// Logisim project MIPS.circ as structural Verilog: 1 circuit, main circuit main
module main (
  input  in_1,
  input  in_2,
  input  [2:0] in_3
);

  wire button_1_out, CLK;
  wire [4:0] rom_1_data_2;
  wire [7:0] adder_1_out, PC_q;
  wire [31:0] alu_1_alu_result, bit_extender_1_out, data_mem_1_rd, regfile32_1_rd1, regfile32_1_rd2,
       rom_1_data;

  Clock clock_1 (.out(CLK));
  Button button_1 (.out(button_1_out));
  Register PC (.D(adder_1_out), .Q(PC_q), .clk(CLK), .clr(button_1_out));  // open: en
  Adder adder_1 (.a(PC_q), .b(8'h4), .out(adder_1_out));  // open: cin, cout
  // Probe on rom_1_data_2
  ROM #(.addrWidth(6), .dataWidth(32)) rom_1 (
    .addr(PC_q[7:2]), .data({rom_1_data[31:26], rom_1_data_2, rom_1_data[20:0]}));  // open: sel
  assign bit_extender_1_out = {{16{rom_1_data[15]}}, rom_1_data[15:0]};  // Bit_Extender bit_extender_1
  RegFile32 regfile32_1 (
    .AD1(rom_1_data_2), .AD2(rom_1_data[20:16]), .CLK(CLK), .WE(in_1), .AD3(rom_1_data[20:16]),
    .WD3(data_mem_1_rd), .RD1(regfile32_1_rd1), .RD2(regfile32_1_rd2));
  // Probe on regfile32_1_rd1
  ALU alu_1 (
    .SrcA(regfile32_1_rd1), .SrcB(bit_extender_1_out), .ALU_Control(in_3), .ALU_Result(alu_1_alu_result));  // open: Zero
  // Probe on regfile32_1_rd2
  Data_Mem data_mem_1 (.A(alu_1_alu_result), .CLK(CLK), .WE(in_2), .WD(regfile32_1_rd2), .RD(data_mem_1_rd));

  // Notes on the sheet:
  //   contents of rom_1 (hex, n*v repeats v):
  //   0 8c080000 ac080001
endmodule
